# Fritzing sketch socket_to_serial (saved by Fritzing 0.7.4b)
breadboards: 1

parts:
  U1 = Arduino Mega
  S3 = Pushbutton [package=THT]
  S4 = Pushbutton [package=THT]
  S5 = Pushbutton [package=THT]
  S6 = Pushbutton [package=THT]
  S7 = Pushbutton [package=THT]
  S8 = Pushbutton [package=THT]
  S9 = Pushbutton [package=THT]
  S10 = Pushbutton [package=THT]
  R1 = Resistor [tolerance=±5% resistance=220 package=THT]
  R2 = Resistor [tolerance=±5% resistance=220 package=THT]
  R3 = Resistor [tolerance=±5% resistance=220 package=THT]
  R4 = Resistor [tolerance=±5% resistance=220 package=THT]
  R5 = Resistor [tolerance=±5% resistance=220 package=THT]
  R6 = Resistor [tolerance=±5% resistance=220 package=THT]
  R7 = Resistor [tolerance=±5% resistance=220 package=THT]
  R8 = Resistor [tolerance=±5% resistance=220 package=THT]
  IC1 = IC, DIP package, 16 pins [chip_label="IC 4051" spacing=300mil]
  LED1 = LED - 5mm [color="Blue (525nm)" package="5 mm [THT]"]

nets:
  N1: U1.GND, IC1.pin6, IC1.pin7, IC1.pin8, LED1.cathode
  N2: U1.D13, LED1.anode
  N3: U1.D0RX, IC1.pin3
  N4: U1.+5V, S3.leg0, S4.leg0, S5.leg0, S6.leg0, S7.leg0, S8.leg0, S9.leg0, S10.leg0, IC1.pin16
  N5: U1.A2, IC1.pin11
  N6: U1.A3, IC1.pin10
  N7: U1.A4, IC1.pin9
  N8: S3.leg1, R1.Pin_1, IC1.pin13
  N9: S4.leg1, R2.Pin_1, IC1.pin14
  N10: S5.leg1, R3.Pin_1, IC1.pin15
  N11: S6.leg1, R4.Pin_1, IC1.pin12
  N12: S7.leg1, R5.Pin_1, IC1.pin1
  N13: S8.leg1, R6.Pin_1, IC1.pin4
  N14: S9.leg1, R7.Pin_1, IC1.pin2
  N15: S10.leg1, R8.Pin_1, IC1.pin5
  N16: R1.Pin_0, R2.Pin_0, R3.Pin_0, R4.Pin_0, R5.Pin_0, R6.Pin_0, R7.Pin_0, R8.Pin_0
